# Fritzing sketch eyes (saved by Fritzing 0.7.4b)
breadboards: 1

parts:
  Arduino1 = Arduino
  R1 = Resistor [tolerance=±5% resistance=330 package=THT]
  LED1 = LED - 5mm [color="Red (633nm)" package="5 mm [THT]"]
  R2 = Resistor [tolerance=±5% resistance=330 package=THT]
  LED2 = LED - 5mm [color="Red (633nm)" package="5 mm [THT]"]
  R3 = Resistor [tolerance=±5% resistance=330 package=THT]
  LED3 = LED - 5mm [color="Red (633nm)" package="5 mm [THT]"]
  R4 = Resistor [tolerance=±5% resistance=330 package=THT]
  LED4 = LED - 5mm [color="Red (633nm)" package="5 mm [THT]"]
  R12 = Resistor [tolerance=±5% resistance=330 package=THT]
  LED12 = LED - 5mm [color="Red (633nm)" package="5 mm [THT]"]
  J1 = male pin header, 7 pins [form="♂ (male)"]
  DC_Power = DC Power [voltage=6]

nets:
  GND: Arduino1.GND, LED1.cathode, LED2.cathode, LED3.cathode, LED4.cathode, LED12.cathode, DC_Power.GND
  N1: Arduino1.D13, R1.Pin_0
  N2: Arduino1.D12, R2.Pin_0
  N3: Arduino1.D11, R3.Pin_0
  N4: Arduino1.D10, R4.Pin_0
  N5: Arduino1.D9, J1.pin1
  N6: Arduino1.D8, J1.pin2
  N7: Arduino1.D7, J1.pin3
  N8: Arduino1.D6, J1.pin4
  N9: Arduino1.D5, J1.pin5
  N10: Arduino1.D4, J1.pin6
  N11: Arduino1.D3, J1.pin7
  N12: Arduino1.D2, R12.Pin_0
  N13: Arduino1.VIN, DC_Power.V+
  N14: R1.Pin_1, LED1.anode
  N15: R2.Pin_1, LED2.anode
  N16: R3.Pin_1, LED3.anode
  N17: R4.Pin_1, LED4.anode
  N18: R12.Pin_1, LED12.anode

notes:
  12 x resistor & LED pairs.
